# Fritzing sketch Ventilatore-LM35-DHT1 (saved by Fritzing 0.9.3b)
breadboards: 1

parts:
  Componente1 = Arduino Uno (Rev3)
  M1 = DC Motor
  D1 = Rectifier Diode [part_number=1N4001 package="300 mil [THT]"]
  Q1 = NPN-Transistor [package="TO92 [THT]"]
  R1 = Resistor [tolerance=±5% resistance=220 package=THT]
  RHT1 = Humidity and Temperature Sensor RHT03

nets:
  N1: Componente1.A0, RHT1.Data-signal
  N2: Componente1.D5_PWM, R1.Pin_1
  N3: M1.pin_1, D1.anode, RHT1.Vcc
  N4: M1.pin_2, D1.cathode, Q1.E
  N5: Q1.B, R1.Pin_0
  N6: Q1.C, RHT1.GND_2
